# Fritzing sketch board_connections (saved by Fritzing 0.9.3b)
breadboards: 1

parts:
  U1 = NodeMCU V1.0
  R1 = Resistor [tolerance=±5% resistance=220 package="2010 [SMD]"]
  LED1 = LED - 3mm [color="Green (570nm)" package="3 mm [THT]"]
  R2 = Resistor [tolerance=±5% resistance=220 package="2010 [SMD]"]
  LED2 = LED - 3mm [color="Red (633nm)" package="3 mm [THT]"]
  U2 = mystery part, 3 pins [chip_label="IR Sensor Front"]
  U3 = mystery part, 4 pins [chip_label="DHT 22"]

nets:
  N1: U1.D1, U3.pin2
  N2: U1.D2, R1.Pin_0
  N3: U1.D3, R2.Pin_0
  N4: U1.3V3, U3.pin1
  N5: U1.GND, R1.Pin_1, LED1.cathode, LED1.anode, R2.Pin_1, LED2.cathode, LED2.anode, U2.pin3, U3.pin4
  N6: U1.Vin, U2.pin2
  N7: U1.A0, U2.pin1

custom parts:
  NodeMCU V1.0: ESP8266 based NodeMCU
